# Fritzing sketch temperature_control_gh (saved by Fritzing 0.9.3b)
circuit board: 8.00336cm x 9.13512cm
breadboards: 2

parts:
  SG1 = Buzzer 12mm [package=buzzer-12mm-ns]
  S1 = Pushbutton [package="[THT]"]
  S2 = Pushbutton [package="[THT]"]
  S3 = Pushbutton [package="[THT]"]
  R3 = Rotary Potentiometer (Small) [maximum_resistance=10kΩ package=THT]
  DS1 = DS18B20 1-Wire Temperature Sensor [part_number=DS18B20]
  Part2 = Arduino Nano (Rev3.0)
  LCD1 = LCD screen
  U1 = RELAY-SOLIDSTATE [package=relay-s108t02]
  LED2 = LED - 3mm [color="Red (633nm)" package="3 mm [THT]"]
  R5 = Resistor [tolerance=±5% resistance=4.7k package=THT]
  R7 = Resistor [tolerance=±5% resistance=440 package=THT]
  R6 = Resistor [tolerance=±5% resistance=220 package=THT]
  R4 = Resistor [tolerance=±5% resistance=220 package=THT]
  R8 = Resistor [tolerance=±5% resistance=4.7k package=THT]

nets:
  N1: SG1.1, Part2.D3
  N2: SG1.2, R4.Pin_1
  N3: S1.Pin_1, S1.Pin_2, Part2.A2
  GND: S1.Pin_3, S1.Pin_4, S2.Pin_3, S2.Pin_4, S3.Pin_3, S3.Pin_4, R3.leg2, DS1.GND, Part2.GND, LCD1.VSS, LCD1.R/W, LCD1.LED-, R6.Pin_1, R4.Pin_0, R8.Pin_0
  N4: S2.Pin_1, S2.Pin_2, Part2.A1
  N5: S3.Pin_1, S3.Pin_2, Part2.A0
  VDD: R3.leg1, DS1.VDD, Part2.5V, LCD1.VDD, R5.Pin_1, R7.Pin_0
  N6: R3.wiper, Part2.A3
  N7: DS1.DQ, Part2.D4, R5.Pin_0
  N8: Part2.D5, U1.+
  N9: Part2.D7, LCD1.E
  N10: Part2.D8, LCD1.RS
  N11: Part2.D9, LCD1.DB7
  N12: Part2.D10, LCD1.DB6
  N13: Part2.D11/MOSI, LCD1.DB5
  N14: Part2.D12/MISO, LCD1.DB4
  N15: LCD1.V0, R8.Pin_1
  N16: LCD1.LED+, R7.Pin_1
  N17: U1.-, LED2.anode
  N18: LED2.cathode, R6.Pin_0
